// Logisim project memmap.circ as structural Verilog: 1 circuit, main circuit main
module main (
  input  in_1
);

  wire and_1_out, and_2_out, and_3_out, and_4_out, and_5_out, and_6_out, and_7_out, and_8_out, and_9_out,
       and_12_out, button_3_out, button_4_out, clk, clkraw, ereg0sel, ereg1sel, ereg2sel, exp0sel, exp1sel,
       exp2sel, expsel, iosel, mclk, mclklatch, not_1_out, not_2_out, not_3_out, not_4_out, not_5_out,
       not_7_out, not_8_out, not_9_out, not_10_out, not_11_out, or_2_out, ramsel, romsel, rst, s_r_ff_1_q,
       s_r_ff_3_q, s_r_ff_4_q;
  wire [7:0] data, register_1_q, register_2_q, register_3_q;
  wire [15:0] addr;

  Counter #(.width(16), .max('hffff)) counter_1 (.Q(addr), .clk(clk), .clr(rst));  // open: load, D, count, carry
  Clock clock_1 (.out(clkraw));
  Button button_1 (.out(rst));
  Button button_2 (.out(mclk));
  not not_1 (not_1_out, clkraw);
  not not_2 (not_2_out, mclklatch);
  and and_1 (and_1_out, mclklatch, clkraw);
  not not_3 (not_3_out, and_1_out);
  not not_4 (not_4_out, and_2_out);
  and and_2 (and_2_out, not_1_out, not_2_out);
  S_R_Flip_Flop s_r_ff_1 (
    .S(mclklatch), .clk(mclk), .R(s_r_ff_1_q), .Q(s_r_ff_1_q), .Qn(mclklatch));  // open: preset, reset, en
  and and_3 (and_3_out, mclklatch, in_1);
  not not_5 (not_5_out, in_1);
  and and_4 (and_4_out, not_5_out, clkraw);
  Button button_3 (.out(button_3_out));
  Button button_4 (.out(button_4_out));
  and and_5 (and_5_out, not_3_out, not_4_out);
  or or_1 (clk, and_3_out, and_4_out);
  S_R_Flip_Flop s_r_ff_2 (.S(button_3_out), .clk(button_4_out), .R(button_4_out));  // open: Q, Qn, preset, reset, en
  S_R_Flip_Flop s_r_ff_3 (.S(and_5_out), .clk(clkraw), .Q(s_r_ff_3_q));  // open: R, Qn, preset, reset, en
  S_R_Flip_Flop s_r_ff_4 (.S(s_r_ff_3_q), .clk(s_r_ff_3_q), .Q(s_r_ff_4_q));  // open: R, Qn, preset, reset, en
  not not_6 (ramsel, addr[15]);
  not not_7 (not_7_out, addr[14]);
  Decoder #(.select(4), .disabled(0)) decoder_1 (
    .out8(ereg0sel), .out9(ereg1sel), .out10(ereg2sel), .sel(addr[3:0]), .en(iosel));  // open: out0, out1, out2, out3, out4, out5, out6, out7, out11, out12, out13, out14, out15
  and and_6 (and_6_out, addr[15], not_7_out);
  not not_8 (not_8_out, addr[12]);
  not not_9 (not_9_out, addr[13]);
  or or_2 (or_2_out, addr[12], addr[13]);
  not not_10 (not_10_out, addr[13]);
  and and_7 (and_7_out, not_10_out, addr[12]);
  and and_8 (and_8_out, addr[13], not_11_out);
  not not_11 (not_11_out, addr[12]);
  and and_9 (and_9_out, addr[13], addr[12]);
  and and_10 (romsel, addr[14], addr[15]);
  and and_11 (iosel, and_6_out, and_12_out);
  and and_12 (and_12_out, not_8_out, not_9_out);
  and and_13 (expsel, and_6_out, or_2_out);
  and and_14 (exp0sel, and_6_out, and_7_out);
  and and_15 (exp1sel, and_6_out, and_8_out);
  and and_16 (exp2sel, and_6_out, and_9_out);
  LED led_1 (.in(ramsel));
  LED led_2 (.in(iosel));
  LED led_3 (.in(expsel));
  LED led_4 (.in(exp0sel));
  LED led_5 (.in(exp1sel));
  LED led_6 (.in(exp2sel));
  LED led_7 (.in(romsel));
  Register register_1 (.D(data), .Q(register_1_q), .clk(ereg0sel), .clr(rst));  // open: en
  Register register_2 (.D(data), .Q(register_2_q), .clk(ereg1sel), .clr(rst));  // open: en
  Register register_3 (.D(data), .Q(register_3_q), .clk(ereg2sel), .clr(rst));  // open: en
  RAM #(.addrWidth(16)) ram_1 (.addr(addr), .data(data), .sel(ramsel), .clk(clk));  // open: ld, clr
  RAM #(.addrWidth(20)) ram_2 (
    .addr({register_1_q, addr[11:0]}), .data(data), .sel(exp0sel), .clk(clk));  // open: ld, clr
  RAM #(.addrWidth(20)) ram_3 (
    .addr({register_2_q, addr[11:0]}), .data(data), .sel(exp1sel), .clk(clk));  // open: ld, clr
  RAM #(.addrWidth(20)) ram_4 (
    .addr({register_3_q, addr[11:0]}), .data(data), .sel(exp2sel), .clk(clk));  // open: ld, clr
  ROM #(.addrWidth(16)) rom_1 (.addr(addr), .data(data), .sel(romsel));
  // also tied to GND on the sheet: {data[0], data[1], data[2], data[3], data[4], data[5], data[6], data[7]}

  // Other names for the same wires on the sheet: mclkmode = in_1
endmodule
